# Fritzing sketch arduino (saved by Fritzing 0.9.5d)
breadboards: 1

parts:
  元件1 = Arduino Due (Rev2b)
  DI1 = 7-Segment LED Display [package=THT]
  R1 = Resistor [tolerance=±5% resistance=220 package=THT]
  R2 = Resistor [tolerance=±5% resistance=10k package=THT]
  S1 = Pushbutton [package="[THT]"]
  J1 = Basic Servo

nets:
  5V: 元件1.5V, S1.Pin_3, S1.Pin_4, J1.vcc
  GND: 元件1.GND, R1.Pin_1, R2.Pin_1, J1.gnd
  N1: 元件1.D8_PWM, DI1.cathodeG
  N2: 元件1.D9_PWM, R2.Pin_0, S1.Pin_1, S1.Pin_2
  N3: 元件1.D10_PWM/SS0, J1.pulse
  N4: 元件1.D2_PWM, DI1.cathodeA
  N5: 元件1.D3_PWM, DI1.cathodeB
  N6: 元件1.D4_PWM/SS1, DI1.cathodeC
  N7: 元件1.D5_PWM, DI1.cathodeD
  N8: 元件1.D6_PWM, DI1.cathodeE
  N9: 元件1.D7_PWM, DI1.cathodeF
  N10: DI1.commAnode#7, R1.Pin_0
